# Fritzing sketch wire-diagram-servo (saved by Fritzing 0.9.3b)
breadboards: 1

parts:
  Part1 = Arduino Uno (Rev3)
  PIR1 = PIR sensor
  S2 = Pushbutton [package="[THT]"]
  R1 = Resistor [tolerance=±5% resistance=10k package=THT]
  J1 = Basic Servo

nets:
  N1: Part1.D2, PIR1.SIG
  N2: Part1.D3_PWM, J1.pulse
  N3: Part1.D5_PWM, S2.Pin_1, S2.Pin_2, R1.Pin_1
  5V: Part1.5V, PIR1.VDD, J1.vcc
  GND: Part1.GND, PIR1.GND, S2.Pin_3, S2.Pin_4, J1.gnd
