# Fritzing sketch wire-diagram (saved by Fritzing 0.9.3b)
breadboards: 1

parts:
  Part1 = Arduino Uno (Rev3)
  PIR1 = PIR sensor
  R1 = Resistor [tolerance=±5% resistance=10k package=THT]
  R2 = Resistor [tolerance=±5% resistance=1k package=THT]
  Q1 = NPN-Transistor [package="TO92 [THT]"]
  S2 = Pushbutton [package="[THT]"]
  Button_in_Glade_Product = Pushbutton [package="[THT]"]

nets:
  N1: Part1.D2, PIR1.SIG
  N2: Part1.D5_PWM, R2.Pin_0
  N3: Part1.D7, R1.Pin_0, S2.Pin_3, S2.Pin_4
  5V: Part1.5V, PIR1.VDD, Q1.C, S2.Pin_1, S2.Pin_2, Button_in_Glade_Product.Pin_1, Button_in_Glade_Product.Pin_2
  GND: Part1.GND, PIR1.GND, R1.Pin_1
  N4: R2.Pin_1, Q1.B
  N5: Q1.E, Button_in_Glade_Product.Pin_3
